// Logisim project Assignment3.circ as structural Verilog
module Decoder (
  input  I0,
  input  I1,
  output F0,
  output F1,
  output F2,
  output F3
);

  wire not_1_out, not_2_out;

  not not_1 (not_1_out, I0);
  not not_2 (not_2_out, I1);
  and and_1 (F0, not_1_out, not_2_out);
  and and_2 (F1, I0, not_2_out);
  and and_3 (F2, not_1_out, I1);
  and and_4 (F3, I0, I1);

  // Notes on the sheet:
  //   I0: pull=down
  //   I1: pull=down
endmodule

module multiplexer (
  input  I1,
  input  I0,
  input  L0,
  input  L1,
  input  L2,
  input  L3,
  output out_7
);

  wire and_1_out, and_2_out, and_3_out, and_4_out, decoder_1_f0, decoder_1_f1, decoder_1_f2, decoder_1_f3;

  Decoder decoder_1 (.I0(I0), .I1(I1), .F0(decoder_1_f0), .F1(decoder_1_f1), .F2(decoder_1_f2), .F3(decoder_1_f3));
  and and_1 (and_1_out, decoder_1_f0, L0);
  and and_2 (and_2_out, decoder_1_f1, L1);
  and and_3 (and_3_out, decoder_1_f2, L2);
  and and_4 (and_4_out, decoder_1_f3, L3);
  or or_1 (out_7, and_1_out, and_2_out, and_3_out, and_4_out);

  // Notes on the sheet:
  //   I1: pull=down
  //   L0: pull=down
  //   L2: pull=down
  //   L3: pull=down
  //   I0: pull=down
  //   L1: pull=down
endmodule

module _4_bit_register (
  input  Clock,
  input  in_2,
  output O0,
  output O1,
  output O2,
  output O3
);

  wire [3:0] undriven;

  D_Flip_Flop d_ff_1 (.clk(Clock), .D(undriven[0]), .Q(O0));  // open: Qn, preset, en, reset
  D_Flip_Flop d_ff_2 (.clk(Clock), .D(undriven[1]), .Q(O1));  // open: Qn, preset, en, reset
  D_Flip_Flop d_ff_3 (.clk(Clock), .D(undriven[2]), .Q(O2));  // open: Qn, preset, en, reset
  D_Flip_Flop d_ff_4 (.clk(Clock), .D(undriven[3]), .Q(O3));  // open: Qn, preset, en, reset
endmodule

module _2_bit_register (
  input  Clock,
  output out_2,
  output out_3
);

  D_Flip_Flop d_ff_1 (.clk(Clock), .Q(out_2));  // open: D, Qn, preset, en, reset
  D_Flip_Flop d_ff_2 (.clk(Clock), .Q(out_3));  // open: D, Qn, preset, en, reset
endmodule
